// Logisim project CPU-jingxiang Zhang.circ as structural Verilog
module \一位全加器  (
  input  X,
  input  Y,
  input  C0,
  output F,
  output Ci
);

  wire and_1_out, and_2_out, and_3_out, xor_1_out;

  xor xor_1 (xor_1_out, X, Y);
  and and_1 (and_1_out, X, Y);
  and and_2 (and_2_out, C0, X);
  and and_3 (and_3_out, Y, C0);
  or or_1 (Ci, and_1_out, and_2_out, and_3_out);
  xor xor_2 (F, xor_1_out, C0);
endmodule

module \带减法的一位全加器  (
  input  Y,
  input  Sub,
  input  X,
  input  C0,
  output Ci,
  output F
);

  wire xor_1_out;

  xor xor_1 (xor_1_out, Y, Sub);
  \一位全加器  \u_一位全加器_1  (.X(X), .Y(xor_1_out), .C0(C0), .F(F), .Ci(Ci));
endmodule

module \_4位ALU  (
  input  [3:0] X,
  input  [3:0] Y,
  input  SUB,
  input  C_in,
  output [3:0] F,
  output C
);

  wire \带减法的一位全加器_2_ci , \带减法的一位全加器_3_ci , \带减法的一位全加器_4_ci ;

  \带减法的一位全加器  \u_带减法的一位全加器_1  (.Y(Y[3]), .Sub(SUB), .X(X[3]), .C0(\带减法的一位全加器_2_ci ), .Ci(C), .F(F[3]));
  \带减法的一位全加器  \u_带减法的一位全加器_2  (.Y(Y[2]), .Sub(SUB), .X(X[2]), .C0(\带减法的一位全加器_3_ci ), .Ci(\带减法的一位全加器_2_ci ), .F(F[2]));
  \带减法的一位全加器  \u_带减法的一位全加器_3  (.Y(Y[1]), .Sub(SUB), .X(X[1]), .C0(\带减法的一位全加器_4_ci ), .Ci(\带减法的一位全加器_3_ci ), .F(F[1]));
  \带减法的一位全加器  \u_带减法的一位全加器_4  (.Y(Y[0]), .Sub(SUB), .X(X[0]), .C0(C_in), .Ci(\带减法的一位全加器_4_ci ), .F(F[0]));
endmodule

module \_8位加法  (
  input  \选中 ,
  input  Sub,
  input  [7:0] X,
  input  [7:0] Y,
  output [7:0] out_5,
  output C
);

  wire \n4位alu_2_c ;
  wire [3:0] \n4位alu_1_f , \n4位alu_2_f ;

  \_4位ALU  \u_4位alu_1  (.F(\n4位alu_1_f ), .X(X[7:4]), .Y(Y[7:4]), .SUB(Sub), .C_in(\n4位alu_2_c ), .C(C));
  and _7 (out_5[7], \选中 , \n4位alu_1_f [3]);
  and _6 (out_5[6], \选中 , \n4位alu_1_f [2]);
  and _5 (out_5[5], \选中 , \n4位alu_1_f [1]);
  and _4 (out_5[4], \选中 , \n4位alu_1_f [0]);
  and _3 (out_5[3], \选中 , \n4位alu_2_f [3]);
  and _2 (out_5[2], \选中 , \n4位alu_2_f [2]);
  and _1 (out_5[1], \选中 , \n4位alu_2_f [1]);
  and _0 (out_5[0], \选中 , \n4位alu_2_f [0]);
  \_4位ALU  \u_4位alu_2  (.F(\n4位alu_2_f ), .X(X[3:0]), .Y(Y[3:0]), .SUB(Sub), .C_in(Sub), .C(\n4位alu_2_c ));
endmodule

module ALU (
  input  S0,
  input  S1,
  input  S2,
  input  [7:0] A,
  input  [7:0] B,
  input  Clock,
  input  ALU_BUS,
  output Carry_out,
  output [7:0] out_9
);

  wire \_8位减法_c , \_8位加法_c , A_A_out, A_B_2_out, A_B_3_out, A_B_4_out, A_B_out, and_1_out, and_2_out,
       not_1_out, not_2_out, not_3_out, not_4_out, not_5_out, not_6_out, not_7_out, not_8_out, not_9_out,
       not_10_out, not_11_out;
  wire [7:0] _0_out, \_8位减法_out_5 , \_8位加法_out_5 , \_8位直通_out_4 , d_ff_1_q, \n8位a与b_1_out_4 ,
       \n8位乘法_采用了multiplier_1_out_4 ;

  assign _0_out = \n8位a与b_1_out_4  | \_8位直通_out_4  | \_8位加法_out_5  | \_8位减法_out_5  | \n8位乘法_采用了multiplier_1_out_4 ;  // OR_Gate _0, 8 bits wide
  not not_1 (not_1_out, S0);
  D_Flip_Flop d_ff_1 (.clk(Clock), .D(_0_out[0]), .Q(d_ff_1_q[0]));  // open: Qn, preset, en, reset
  assign out_9 = ALU_BUS ? d_ff_1_q : 8'bz;  // Controlled_Buffer controlled_buffer_1
  not not_2 (not_2_out, S1);
  not not_3 (not_3_out, S2);
  and A_B (A_B_out, not_1_out, not_2_out, not_3_out);
  \_8位A与B  \u_8位a与b_1  (.A(A), .B(B), .\高有效 (A_B_out), .out_4(\n8位a与b_1_out_4 ));
  D_Flip_Flop d_ff_2 (.clk(Clock), .D(_0_out[1]), .Q(d_ff_1_q[1]));  // open: Qn, preset, en, reset
  not not_4 (not_4_out, S1);
  and A_A (A_A_out, S0, not_4_out, not_5_out);
  D_Flip_Flop d_ff_3 (.clk(Clock), .D(_0_out[2]), .Q(d_ff_1_q[2]));  // open: Qn, preset, en, reset
  not not_5 (not_5_out, S2);
  \_8位A与B  \_8位直通  (.A(A), .B(A), .\高有效 (A_A_out), .out_4(\_8位直通_out_4 ));
  D_Flip_Flop d_ff_4 (.clk(Clock), .D(_0_out[3]), .Q(d_ff_1_q[3]));  // open: Qn, preset, en, reset
  not not_6 (not_6_out, S2);
  not not_7 (not_7_out, S0);
  and A_B_2 (A_B_2_out, not_7_out, S1, not_6_out);
  not not_8 (not_8_out, A_B_2_out);
  \_8位加法  \_8位加法  (.out_5(\_8位加法_out_5 ), .Sub(not_8_out), .X(A), .Y(B), .C(\_8位加法_c ), .\选中 (A_B_2_out));
  D_Flip_Flop d_ff_5 (.clk(Clock), .D(_0_out[4]), .Q(d_ff_1_q[4]));  // open: Qn, preset, en, reset
  and and_1 (and_1_out, \_8位加法_c , A_B_2_out);
  D_Flip_Flop d_ff_6 (.clk(Clock), .D(_0_out[5]), .Q(d_ff_1_q[5]));  // open: Qn, preset, en, reset
  not not_9 (not_9_out, S2);
  and A_B_3 (A_B_3_out, S0, S1, not_9_out);
  \_8位加法  \_8位减法  (.out_5(\_8位减法_out_5 ), .Sub(A_B_3_out), .X(A), .Y(B), .C(\_8位减法_c ), .\选中 (A_B_3_out));
  D_Flip_Flop d_ff_7 (.clk(Clock), .D(_0_out[6]), .Q(d_ff_1_q[6]));  // open: Qn, preset, en, reset
  not not_10 (not_10_out, S0);
  and and_2 (and_2_out, \_8位减法_c , A_B_3_out);
  D_Flip_Flop d_ff_8 (.clk(Clock), .D(_0_out[7]), .Q(d_ff_1_q[7]));  // open: Qn, preset, en, reset
  not not_11 (not_11_out, S1);
  and A_B_4 (A_B_4_out, not_10_out, not_11_out, S2);
  \_8位乘法_采用了Multiplier  \u_8位乘法_采用了multiplier_1  (
    .out_4(\n8位乘法_采用了multiplier_1_out_4 ), .A(A), .B(B), .\选中 (A_B_4_out));
  or _0_2 (Carry_out, and_1_out, and_2_out);
endmodule

module \_8位A与B  (
  input  [7:0] A,
  input  [7:0] B,
  input  \高有效 ,
  output [7:0] out_4
);

  wire _0_out, _1_out, _2_out, _3_2_out, _4_out, _5_out, _6_out, _7_2_out;

  or _0 (_0_out, A[0], B[0]);
  and _0_2 (out_4[0], \高有效 , _0_out);
  or _1 (_1_out, A[1], B[1]);
  and _1_2 (out_4[1], \高有效 , _1_out);
  or _2 (_2_out, A[2], B[2]);
  and _2_2 (out_4[2], \高有效 , _2_out);
  and _3 (out_4[3], \高有效 , _3_2_out);
  or _3_2 (_3_2_out, A[3], B[3]);
  or _4 (_4_out, A[4], B[4]);
  and _4_2 (out_4[4], \高有效 , _4_out);
  or _5 (_5_out, A[5], B[5]);
  and _5_2 (out_4[5], \高有效 , _5_out);
  or _6 (_6_out, A[6], B[6]);
  and _7 (out_4[7], \高有效 , _7_2_out);
  and _6_2 (out_4[6], \高有效 , _6_out);
  or _7_2 (_7_2_out, A[7], B[7]);
endmodule

module \_8位乘法_采用了Multiplier  (
  input  [7:0] A,
  input  [7:0] B,
  input  \选中 ,
  output [7:0] out_4
);

  wire [7:0] multiplier_1_out;

  Multiplier multiplier_1 (.a({4'b0000, B[3:0]}), .b({4'b0000, A[3:0]}), .out(multiplier_1_out));  // open: cin, cout
  and _7 (out_4[7], \选中 , multiplier_1_out[7]);
  and _6 (out_4[6], \选中 , multiplier_1_out[6]);
  and _5 (out_4[5], \选中 , multiplier_1_out[5]);
  and _4 (out_4[4], \选中 , multiplier_1_out[4]);
  and _3 (out_4[3], \选中 , multiplier_1_out[3]);
  and _2 (out_4[2], \选中 , multiplier_1_out[2]);
  and _1 (out_4[1], \选中 , multiplier_1_out[1]);
  and _0 (out_4[0], \选中 , multiplier_1_out[0]);
endmodule

module \数据通路  (
  input  in_1,
  input  in_2,
  input  in_3,
  input  in_4,
  input  in_5,
  input  in_6,
  input  in_7,
  input  in_8,
  input  in_9,
  input  in_10,
  input  in_11,
  input  in_12,
  input  in_13,
  input  in_14,
  input  in_15,
  input  in_16,
  input  in_17,
  input  in_18,
  input  in_19,
  input  in_20,
  input  in_21,
  input  in_22,
  input  in_23,
  input  in_24,
  input  in_25,
  input  in_26,
  input  in_27,
  input  in_28,
  input  in_29,
  input  in_30,
  input  [7:0] in_31,
  input  in_32,
  input  in_33,
  input  in_34,
  input  in_35,
  input  in_36,
  input  in_37,
  output [7:0] DUBS,
  output [7:0] \指令通路 ,
  output [7:0] out_40,
  output [7:0] AR2,
  output [7:0] \B端口 ,
  output [7:0] out_43,
  output [7:0] out_44,
  output [7:0] out_45,
  output [7:0] out_46,
  output [7:0] out_47,
  output [7:0] PC,
  output [7:0] out_49,
  output [7:0] out_50,
  output [7:0] out_51,
  output [7:0] out_52,
  output [7:0] out_53,
  output [7:0] out_54,
  output [7:0] out_55
);

  wire ALU_BUS, AR1_INC, CEL, CER, IAR_BUS, LDAR1, LDAR2, LDDR1, LDDR2, LDER, LDIAR, LDIR, LDPC, LDR4, LRW,
       M1, M2, M3, M4, not_1_out, not_2_out, not_3_out, not_4_out, not_6_out, or_1_out, PC_ADD_INC, RD0, RD1,
       RS0, RS1, RS_BUS, S0, S1, S2, SW_BUS, WR0, WR1, WRD, \自动控制 ;
  wire [3:0] \控制字段 ;
  wire [4:0] \内存控制 ;
  wire [5:0] \BUS控制 , \取指控制 , \微地址 ;
  wire [6:0] \ALU控制 ;
  wire [7:0] \RF控制 ;

  assign DUBS = RS_BUS ? out_45 : 8'bz;  // Controlled_Buffer controlled_buffer_1
  assign RS_BUS = not_2_out ? \BUS控制 [5] : 1'bz;  // Controlled_Buffer controlled_buffer_2
  assign LDIR = not_1_out ? \取指控制 [5] : 1'bz;  // Controlled_Buffer controlled_buffer_3
  assign M4 = not_1_out ? \取指控制 [4] : 1'bz;  // Controlled_Buffer controlled_buffer_4
  \带时钟的数据选择器  \u_带时钟的数据选择器_1  (.X2(DUBS), .X1(out_45), .\选择 (M1), .T(in_16), .out_6(\B端口 ), .LDDR(LDDR1));
  assign SW_BUS = not_2_out ? \BUS控制 [4] : 1'bz;  // Controlled_Buffer controlled_buffer_5
  assign LDR4 = not_1_out ? \取指控制 [3] : 1'bz;  // Controlled_Buffer controlled_buffer_6
  \带时钟的寄存器  \u_带时钟的寄存器_1  (.in_1(DUBS), .T(in_16), .out_5(out_50), .LDER(LDER), .clear(in_15));
  assign DUBS = SW_BUS ? in_31 : 8'bz;  // Controlled_Buffer controlled_buffer_7
  assign CEL = not_2_out ? \BUS控制 [2] : 1'bz;  // Controlled_Buffer controlled_buffer_8
  assign ALU_BUS = not_2_out ? \BUS控制 [3] : 1'bz;  // Controlled_Buffer controlled_buffer_9
  assign LDIAR = not_1_out ? \取指控制 [1] : 1'bz;  // Controlled_Buffer controlled_buffer_10
  assign LDPC = not_1_out ? \取指控制 [2] : 1'bz;  // Controlled_Buffer controlled_buffer_11
  ALU ALU (
    .S0(S0), .S1(S1), .S2(S2), .A(out_43), .B(\B端口 ), .Clock(in_16), .ALU_BUS(ALU_BUS), .out_9(DUBS));  // open: Carry_out
  \带时钟的数据选择器  \u_带时钟的数据选择器_2  (.X2(DUBS), .X1(out_46), .\选择 (M2), .T(in_16), .out_6(out_43), .LDDR(LDDR2));
  \寄存器组RF  \u_寄存器组rf_1  (
    .WR1(WR1), .WR0(WR0), .RS1(RS1), .RS0(RS0), .RD1(RD1), .RD0(RD0), .WRD(WRD), .T(in_16), .Clear(in_15),
    .\B端口 (out_45), .\A端口 (out_46), .IN(out_50));
  assign CER = not_2_out ? \BUS控制 [1] : 1'bz;  // Controlled_Buffer controlled_buffer_12
  assign PC_ADD_INC = not_1_out ? \取指控制 [0] : 1'bz;  // Controlled_Buffer controlled_buffer_13
  assign IAR_BUS = not_2_out ? \BUS控制 [0] : 1'bz;  // Controlled_Buffer controlled_buffer_14
  not not_1 (not_1_out, \自动控制 );
  not not_2 (not_2_out, \自动控制 );
  assign LRW = not_3_out ? \内存控制 [4] : 1'bz;  // Controlled_Buffer controlled_buffer_15
  assign RD0 = not_4_out ? \RF控制 [6] : 1'bz;  // Controlled_Buffer controlled_buffer_16
  assign RD1 = not_4_out ? \RF控制 [7] : 1'bz;  // Controlled_Buffer controlled_buffer_17
  assign AR1_INC = not_3_out ? \内存控制 [3] : 1'bz;  // Controlled_Buffer controlled_buffer_18
  assign DUBS = IAR_BUS ? out_47 : 8'bz;  // Controlled_Buffer controlled_buffer_19
  \高电平触发的锁存器  \u_高电平触发的锁存器_1  (.LDIAR(or_1_out), .in_2(out_44), .out_3(out_47));
  or or_1 (or_1_out, LDIAR, in_15);
  assign RS1 = not_4_out ? \RF控制 [5] : 1'bz;  // Controlled_Buffer controlled_buffer_20
  assign RS0 = not_4_out ? \RF控制 [4] : 1'bz;  // Controlled_Buffer controlled_buffer_21
  assign M3 = not_3_out ? \内存控制 [1] : 1'bz;  // Controlled_Buffer controlled_buffer_22
  assign LDAR1 = not_3_out ? \内存控制 [2] : 1'bz;  // Controlled_Buffer controlled_buffer_23
  AR1 ar1_1 (.LDAR(LDAR1), .in_4(DUBS), .AR1_INC(AR1_INC), .out_5(out_40), .T(in_16));
  \控制器  \u_控制器_1  (
    .T(in_16), .IR(out_51), .\内存控制 (\内存控制 ), .\取值控制 (\取指控制 ), .\UBS控制 (\BUS控制 ), .\AUL计算控制 (\ALU控制 ),
    .\RF存储器控制 (\RF控制 ), .\控制字段 (\控制字段 ), .\地址转移 (\微地址 ), .Clear(in_15), .SW(in_23));
  assign WR1 = not_4_out ? \RF控制 [3] : 1'bz;  // Controlled_Buffer controlled_buffer_24
  assign WR0 = not_4_out ? \RF控制 [2] : 1'bz;  // Controlled_Buffer controlled_buffer_25
  assign LDAR2 = not_3_out ? \内存控制 [0] : 1'bz;  // Controlled_Buffer controlled_buffer_26
  not not_3 (not_3_out, \自动控制 );
  RAM ram_1 (
    .L_address(out_40), .LRW(LRW), .T(in_16), .Clear(in_15), .R_address(AR2), .\数据流出 (DUBS), .\数据进入 (DUBS),
    .\指令端口 (out_54), .CER(CER), .nCEL(CEL));
  assign LDER = not_4_out ? \RF控制 [0] : 1'bz;  // Controlled_Buffer controlled_buffer_27
  assign WRD = not_4_out ? \RF控制 [1] : 1'bz;  // Controlled_Buffer controlled_buffer_28
  \带时钟的数据选择器  \u_带时钟的数据选择器_3  (.X2(DUBS), .X1(out_44), .\选择 (M3), .T(in_16), .out_6(AR2), .LDDR(LDAR2));
  \带时钟的寄存器  \u_带时钟的寄存器_2  (.in_1(PC), .T(in_16), .out_5(out_44), .LDER(LDPC), .clear(in_15));
  ALU2 alu2_1 (.PC_ADD_INC(PC_ADD_INC), .IAR_IN(out_44), .R4_IN(out_49), .out_4(PC));
  \带时钟的数据选择器  \u_带时钟的数据选择器_4  (.X2(DUBS), .X1(out_51), .\选择 (M4), .T(in_16), .out_6(out_49), .LDDR(LDR4));
  \带时钟的寄存器  \u_带时钟的寄存器_3  (.in_1(out_54), .T(in_16), .out_5(out_51), .LDER(LDIR), .clear(in_15));
  not not_4 (not_4_out, \自动控制 );
  assign LDDR1 = not_6_out ? \ALU控制 [5] : 1'bz;  // Controlled_Buffer controlled_buffer_29
  assign M1 = not_6_out ? \ALU控制 [6] : 1'bz;  // Controlled_Buffer controlled_buffer_30
  assign M2 = not_6_out ? \ALU控制 [4] : 1'bz;  // Controlled_Buffer controlled_buffer_31
  assign LDDR2 = not_6_out ? \ALU控制 [3] : 1'bz;  // Controlled_Buffer controlled_buffer_32
  not not_5 (\自动控制 , in_32);
  assign S0 = not_6_out ? \ALU控制 [2] : 1'bz;  // Controlled_Buffer controlled_buffer_33
  assign S1 = not_6_out ? \ALU控制 [1] : 1'bz;  // Controlled_Buffer controlled_buffer_34
  assign RS_BUS = \自动控制  ? in_1 : 1'bz;  // Controlled_Buffer controlled_buffer_35
  assign RD1 = \自动控制  ? in_7 : 1'bz;  // Controlled_Buffer controlled_buffer_36
  assign LDIR = \自动控制  ? in_17 : 1'bz;  // Controlled_Buffer controlled_buffer_37
  assign S2 = not_6_out ? \ALU控制 [0] : 1'bz;  // Controlled_Buffer controlled_buffer_38
  not not_6 (not_6_out, \自动控制 );
  assign ALU_BUS = \自动控制  ? in_3 : 1'bz;  // Controlled_Buffer controlled_buffer_39
  assign SW_BUS = \自动控制  ? in_2 : 1'bz;  // Controlled_Buffer controlled_buffer_40
  assign RS1 = \自动控制  ? in_9 : 1'bz;  // Controlled_Buffer controlled_buffer_41
  assign RD0 = \自动控制  ? in_8 : 1'bz;  // Controlled_Buffer controlled_buffer_42
  assign LDR4 = \自动控制  ? in_19 : 1'bz;  // Controlled_Buffer controlled_buffer_43
  assign M4 = \自动控制  ? in_18 : 1'bz;  // Controlled_Buffer controlled_buffer_44
  assign M1 = \自动控制  ? in_24 : 1'bz;  // Controlled_Buffer controlled_buffer_45
  assign LRW = \自动控制  ? in_33 : 1'bz;  // Controlled_Buffer controlled_buffer_46
  assign CEL = \自动控制  ? in_4 : 1'bz;  // Controlled_Buffer controlled_buffer_47
  assign RS0 = \自动控制  ? in_10 : 1'bz;  // Controlled_Buffer controlled_buffer_48
  assign WR1 = \自动控制  ? in_11 : 1'bz;  // Controlled_Buffer controlled_buffer_49
  assign LDPC = \自动控制  ? in_20 : 1'bz;  // Controlled_Buffer controlled_buffer_50
  assign LDDR1 = \自动控制  ? in_25 : 1'bz;  // Controlled_Buffer controlled_buffer_51
  assign M2 = \自动控制  ? in_26 : 1'bz;  // Controlled_Buffer controlled_buffer_52
  assign AR1_INC = \自动控制  ? in_34 : 1'bz;  // Controlled_Buffer controlled_buffer_53
  assign CER = \自动控制  ? in_5 : 1'bz;  // Controlled_Buffer controlled_buffer_54
  assign WRD = \自动控制  ? in_13 : 1'bz;  // Controlled_Buffer controlled_buffer_55
  assign WR0 = \自动控制  ? in_12 : 1'bz;  // Controlled_Buffer controlled_buffer_56
  assign LDIAR = \自动控制  ? in_21 : 1'bz;  // Controlled_Buffer controlled_buffer_57
  assign LDDR2 = \自动控制  ? in_27 : 1'bz;  // Controlled_Buffer controlled_buffer_58
  assign S0 = \自动控制  ? in_28 : 1'bz;  // Controlled_Buffer controlled_buffer_59
  assign M3 = \自动控制  ? in_36 : 1'bz;  // Controlled_Buffer controlled_buffer_60
  assign LDAR1 = \自动控制  ? in_35 : 1'bz;  // Controlled_Buffer controlled_buffer_61
  assign IAR_BUS = \自动控制  ? in_6 : 1'bz;  // Controlled_Buffer controlled_buffer_62
  assign LDER = \自动控制  ? in_14 : 1'bz;  // Controlled_Buffer controlled_buffer_63
  assign PC_ADD_INC = \自动控制  ? in_22 : 1'bz;  // Controlled_Buffer controlled_buffer_64
  assign S2 = \自动控制  ? in_30 : 1'bz;  // Controlled_Buffer controlled_buffer_65
  assign S1 = \自动控制  ? in_29 : 1'bz;  // Controlled_Buffer controlled_buffer_66
  assign LDAR2 = \自动控制  ? in_37 : 1'bz;  // Controlled_Buffer controlled_buffer_67

  assign out_52 = DUBS;
  assign out_53 = out_40;
  assign out_55 = AR2;
  assign \指令通路  = out_54;

  // Other names for the same wires on the sheet: AR1[7:0] = out_40; restart = in_15; SW = in_23; T = in_16

  // Notes on the sheet:
  //   S0
  //   S1
  //   S2
  //   C
  //   DR1
  //   MUX1
  //   B端口
  //   RF
  //   ER
  //   SW7~SW0
  //   T
  //   ALU_BUS
  //   A端口
  //   DR2
  //   MUX2
  //   A端口
  //   BUS控制
  //   指令控制
  //   DBUS
  //   控制器
  //   数据端口
  //   AR1
  //   IAR
  //   指令端口
  //   RAM
  //   内存控制
  //   MUX3
  //   R4
  //   RF存储器
  //   ALU2
  //   MUX4
  //   IR
  //   ALU计算
  //   一键重启
  //   全局时钟
  //   用于自动控制写入RAM
  //   用于控制器自动控制
  //   手动控制
  //   BUS控制
  //   RF存储器
  //   指令控制
  //   ALU计算
  //   内存控制
endmodule

module \带时钟的数据选择器  (
  input  [7:0] X2,
  input  [7:0] X1,
  input  \选择 ,
  input  T,
  input  LDDR,
  output [7:0] out_6
);

  wire and_1_out, not_1_out;
  wire [7:0] _0_out, bitselector_1_out, bitselector_2_out;

  and and_1 (and_1_out, T, LDDR);
  not not_1 (not_1_out, \选择 );
  D_Flip_Flop d_ff_1 (.clk(and_1_out), .D(_0_out[0]), .Q(out_6[0]));  // open: Qn, preset, en, reset
  BitSelector #(.group(8)) bitselector_1 (.in(X2), .out(bitselector_1_out), .sel(not_1_out));
  BitSelector #(.group(8)) bitselector_2 (.in(X1), .out(bitselector_2_out), .sel(\选择 ));
  D_Flip_Flop d_ff_2 (.clk(and_1_out), .D(_0_out[1]), .Q(out_6[1]));  // open: Qn, preset, en, reset
  D_Flip_Flop d_ff_3 (.clk(and_1_out), .D(_0_out[2]), .Q(out_6[2]));  // open: Qn, preset, en, reset
  assign _0_out = bitselector_1_out | bitselector_2_out;  // OR_Gate _0, 8 bits wide
  D_Flip_Flop d_ff_4 (.clk(and_1_out), .D(_0_out[3]), .Q(out_6[3]));  // open: Qn, preset, en, reset
  D_Flip_Flop d_ff_5 (.clk(and_1_out), .D(_0_out[4]), .Q(out_6[4]));  // open: Qn, preset, en, reset
  D_Flip_Flop d_ff_6 (.clk(and_1_out), .D(_0_out[5]), .Q(out_6[5]));  // open: Qn, preset, en, reset
  D_Flip_Flop d_ff_7 (.clk(and_1_out), .D(_0_out[6]), .Q(out_6[6]));  // open: Qn, preset, en, reset
  D_Flip_Flop d_ff_8 (.clk(and_1_out), .D(_0_out[7]), .Q(out_6[7]));  // open: Qn, preset, en, reset
endmodule

module \寄存器组RF  (
  input  WR1,
  input  WR0,
  input  RS1,
  input  RS0,
  input  RD1,
  input  RD0,
  input  WRD,
  input  [7:0] IN,
  input  T,
  input  Clear,
  output [7:0] \B端口 ,
  output [7:0] \A端口 
);

  wire and_1_out, and_2_out, and_3_out, and_4_out, and_5_out, and_6_out, and_7_out, and_8_out, and_9_out,
       and_10_out, and_11_out, and_12_out, and_13_out, and_14_out, and_15_out, and_16_out, and_17_out,
       and_18_out, and_19_out, and_20_out, and_21_out, and_22_out, and_23_out, and_24_out, and_25_out,
       and_26_out, and_27_out, and_28_out, and_29_out, and_30_out, and_31_out, and_32_out, not_1_out,
       not_2_out, not_3_out, not_4_out, not_5_out, not_6_out, not_7_out, not_8_out, not_9_out, not_10_out,
       not_11_out, not_12_out, not_13_out, not_14_out, not_15_out, not_16_out, not_17_out, not_18_out,
       not_19_out, not_20_out, not_21_out, or_1_out, or_2_out, or_3_out, or_4_out;
  wire [7:0] ram_1_data, ram_2_data, ram_3_data, ram_4_data;

  not not_1 (not_1_out, WRD);
  not not_2 (not_2_out, WR0);
  not not_3 (not_3_out, WR0);
  not not_4 (not_4_out, WR1);
  and and_1 (and_1_out, not_4_out, not_2_out);
  and and_2 (and_2_out, WR1, not_3_out);
  and and_3 (and_3_out, and_1_out, WRD);
  and and_4 (and_4_out, and_2_out, WRD);
  not not_5 (not_5_out, WR1);
  and and_5 (and_5_out, WR1, WR0);
  and and_6 (and_6_out, not_5_out, WR0);
  and and_7 (and_7_out, and_6_out, WRD);
  and and_8 (and_8_out, and_5_out, WRD);
  or or_1 (or_1_out, and_3_out, and_11_out, and_17_out);
  not not_6 (not_6_out, RS1);
  not not_7 (not_7_out, RS0);
  and and_9 (and_9_out, RS1, not_8_out);
  and and_10 (and_10_out, not_6_out, not_7_out);
  and and_11 (and_11_out, and_10_out, not_1_out);
  or or_2 (or_2_out, and_4_out, and_14_out, and_22_out);
  RAM_part #(.addrWidth(2)) ram_1 (
    .addr(2'b00), .data(ram_1_data), .sel(or_1_out), .clk(T), .ld(not_1_out), .clr(Clear));
  RAM_part #(.addrWidth(2)) ram_2 (
    .addr(2'b00), .data(ram_2_data), .sel(or_2_out), .clk(T), .ld(not_1_out), .clr(Clear));
  not not_8 (not_8_out, RS0);
  not not_9 (not_9_out, RS1);
  and and_12 (and_12_out, RS1, RS0);
  and and_13 (and_13_out, not_9_out, RS0);
  and and_14 (and_14_out, and_9_out, not_1_out);
  and and_15 (and_15_out, and_13_out, not_1_out);
  or or_3 (or_3_out, and_7_out, and_15_out, and_21_out);
  not not_10 (not_10_out, RD1);
  not not_11 (not_11_out, RD0);
  and and_16 (and_16_out, not_10_out, not_11_out);
  and and_17 (and_17_out, and_16_out, not_1_out);
  and and_18 (and_18_out, and_12_out, not_1_out);
  or or_4 (or_4_out, and_8_out, and_18_out, and_24_out);
  not not_12 (not_12_out, RD1);
  not not_13 (not_13_out, RD0);
  and and_19 (and_19_out, not_12_out, RD0);
  and and_20 (and_20_out, RD1, not_13_out);
  and and_21 (and_21_out, and_19_out, not_1_out);
  and and_22 (and_22_out, and_20_out, not_1_out);
  RAM_part #(.addrWidth(2)) ram_3 (
    .addr(2'b00), .data(ram_3_data), .sel(or_3_out), .clk(T), .ld(not_1_out), .clr(Clear));
  RAM_part #(.addrWidth(2)) ram_4 (
    .addr(2'b00), .data(ram_4_data), .sel(or_4_out), .clk(T), .ld(not_1_out), .clr(Clear));
  and and_23 (and_23_out, RD1, RD0);
  and and_24 (and_24_out, and_23_out, not_1_out);
  not not_14 (not_14_out, RS1);
  and and_25 (and_25_out, not_14_out, not_17_out);
  assign ram_1_data = WRD ? IN : 8'bz;  // Controlled_Buffer controlled_buffer_1
  assign ram_3_data = WRD ? IN : 8'bz;  // Controlled_Buffer controlled_buffer_2
  assign ram_2_data = WRD ? IN : 8'bz;  // Controlled_Buffer controlled_buffer_3
  assign ram_4_data = WRD ? IN : 8'bz;  // Controlled_Buffer controlled_buffer_4
  not not_15 (not_15_out, RS1);
  not not_16 (not_16_out, RS0);
  not not_17 (not_17_out, RS0);
  and and_26 (and_26_out, not_15_out, RS0);
  and and_27 (and_27_out, RS1, not_16_out);
  assign \B端口  = and_27_out ? ram_2_data : 8'bz;  // Controlled_Buffer controlled_buffer_5
  assign \B端口  = and_25_out ? ram_1_data : 8'bz;  // Controlled_Buffer controlled_buffer_6
  and and_28 (and_28_out, RS1, RS0);
  assign \B端口  = and_26_out ? ram_3_data : 8'bz;  // Controlled_Buffer controlled_buffer_7
  assign \B端口  = and_28_out ? ram_4_data : 8'bz;  // Controlled_Buffer controlled_buffer_8
  not not_18 (not_18_out, RD0);
  not not_19 (not_19_out, RD1);
  and and_29 (and_29_out, not_19_out, not_18_out);
  assign \A端口  = and_29_out ? ram_1_data : 8'bz;  // Controlled_Buffer controlled_buffer_9
  not not_20 (not_20_out, RD1);
  not not_21 (not_21_out, RD0);
  and and_30 (and_30_out, not_20_out, RD0);
  and and_31 (and_31_out, RD1, not_21_out);
  assign \A端口  = and_30_out ? ram_3_data : 8'bz;  // Controlled_Buffer controlled_buffer_10
  assign \A端口  = and_31_out ? ram_2_data : 8'bz;  // Controlled_Buffer controlled_buffer_11
  and and_32 (and_32_out, RD1, RD0);
  assign \A端口  = and_32_out ? ram_4_data : 8'bz;  // Controlled_Buffer controlled_buffer_12
endmodule

module \带时钟的寄存器  (
  input  [7:0] in_1,
  input  T,
  input  LDER,
  input  clear,
  output [7:0] out_5
);

  wire and_1_out;

  and and_1 (and_1_out, T, LDER);
  D_Flip_Flop d_ff_1 (.clk(and_1_out), .D(in_1[0]), .Q(out_5[0]), .reset(clear));  // open: Qn, preset, en
  D_Flip_Flop d_ff_2 (.clk(and_1_out), .D(in_1[1]), .Q(out_5[1]), .reset(clear));  // open: Qn, preset, en
  D_Flip_Flop d_ff_3 (.clk(and_1_out), .D(in_1[2]), .Q(out_5[2]), .reset(clear));  // open: Qn, preset, en
  D_Flip_Flop d_ff_4 (.clk(and_1_out), .D(in_1[3]), .Q(out_5[3]), .reset(clear));  // open: Qn, preset, en
  D_Flip_Flop d_ff_5 (.clk(and_1_out), .D(in_1[4]), .Q(out_5[4]), .reset(clear));  // open: Qn, preset, en
  D_Flip_Flop d_ff_6 (.clk(and_1_out), .D(in_1[5]), .Q(out_5[5]), .reset(clear));  // open: Qn, preset, en
  D_Flip_Flop d_ff_7 (.clk(and_1_out), .D(in_1[6]), .Q(out_5[6]), .reset(clear));  // open: Qn, preset, en
  D_Flip_Flop d_ff_8 (.clk(and_1_out), .D(in_1[7]), .Q(out_5[7]), .reset(clear));  // open: Qn, preset, en
endmodule

module RAM (
  input  nCEL,
  input  [7:0] L_address,
  input  [7:0] \数据进入 ,
  input  LRW,
  input  T,
  input  Clear,
  input  CER,
  input  [7:0] R_address,
  output [7:0] \数据流出 ,
  output [7:0] \指令端口 
);

  wire and_1_out, not_1_out, not_2_out, not_3_out;
  wire [7:0] controlled_buffer_1_out, controlled_buffer_7_out, ram_1_data, ram_2_data;

  assign controlled_buffer_1_out = LRW ? L_address : 8'bz;  // Controlled_Buffer controlled_buffer_1
  not not_1 (not_1_out, LRW);
  assign controlled_buffer_1_out = not_1_out ? R_address : 8'bz;  // Controlled_Buffer controlled_buffer_2
  not not_2 (not_2_out, not_1_out);
  RAM_part ram_1 (.addr(L_address), .data(ram_1_data), .clk(T), .ld(not_1_out), .clr(Clear));  // open: sel
  RAM_part ram_2 (
    .addr(controlled_buffer_1_out), .data(ram_2_data), .clk(T), .ld(not_1_out), .clr(Clear));  // open: sel
  not not_3 (not_3_out, not_1_out);
  assign ram_2_data = not_3_out ? ram_1_data : 8'bz;  // Controlled_Buffer controlled_buffer_3
  and and_1 (and_1_out, not_2_out, nCEL);
  assign ram_1_data = and_1_out ? \数据进入  : 8'bz;  // Controlled_Buffer controlled_buffer_4
  assign \指令端口  = CER ? ram_2_data : 8'bz;  // Controlled_Buffer controlled_buffer_5
  assign \数据流出  = not_1_out ? controlled_buffer_7_out : 8'bz;  // Controlled_Buffer controlled_buffer_6
  assign controlled_buffer_7_out = nCEL ? ram_1_data : 8'bz;  // Controlled_Buffer controlled_buffer_7
endmodule

module AR1 (
  input  AR1_INC,
  input  LDAR,
  input  T,
  input  [7:0] in_4,
  output [7:0] out_5
);

  wire not_1_out, or_1_out;
  wire [7:0] adder_1_out, controlled_buffer_1_out;

  or or_1 (or_1_out, LDAR, AR1_INC);
  \带时钟的寄存器  \u_带时钟的寄存器_1  (.in_1(controlled_buffer_1_out), .T(T), .out_5(out_5), .LDER(or_1_out));  // open: clear
  assign controlled_buffer_1_out = not_1_out ? in_4 : 8'bz;  // Controlled_Buffer controlled_buffer_1
  not not_1 (not_1_out, AR1_INC);
  Adder adder_1 (.a(8'h1), .b(out_5), .out(adder_1_out), .cin(1'b0));  // open: cout
  assign controlled_buffer_1_out = AR1_INC ? adder_1_out : 8'bz;  // Controlled_Buffer controlled_buffer_2
endmodule

module \高电平触发的锁存器  (
  input  LDIAR,
  input  [7:0] in_2,
  output [7:0] out_3
);

  wire not_2_out;
  wire [7:0] and_1_out, and_2_out, controlled_buffer_1_out, not_1_out, not_4_out, or_1_out, or_2_out;

  assign not_1_out = ~in_2;  // NOT_Gate not_1, 8 bits wide
  not not_2 (not_2_out, LDIAR);
  assign controlled_buffer_1_out = LDIAR ? {8{1'b1}} : 8'bz;  // Controlled_Buffer controlled_buffer_1
  assign controlled_buffer_1_out = not_2_out ? {8{1'b0}} : 8'bz;  // Controlled_Buffer controlled_buffer_2
  assign and_1_out = controlled_buffer_1_out & not_1_out;  // AND_Gate and_1, 8 bits wide
  assign and_2_out = controlled_buffer_1_out & in_2;  // AND_Gate and_2, 8 bits wide
  assign or_1_out = and_1_out | not_4_out;  // OR_Gate or_1, 8 bits wide
  assign or_2_out = out_3 | and_2_out;  // OR_Gate or_2, 8 bits wide
  assign out_3 = ~or_1_out;  // NOT_Gate not_3, 8 bits wide
  assign not_4_out = ~or_2_out;  // NOT_Gate not_4, 8 bits wide
endmodule

module ALU2 (
  input  PC_ADD_INC,
  input  [7:0] IAR_IN,
  input  [7:0] R4_IN,
  output [7:0] out_4
);

  wire not_1_out;
  wire [7:0] controlled_buffer_1_out;

  not not_1 (not_1_out, PC_ADD_INC);
  assign controlled_buffer_1_out = PC_ADD_INC ? 8'h1 : 8'bz;  // Controlled_Buffer controlled_buffer_1
  assign controlled_buffer_1_out = not_1_out ? R4_IN : 8'bz;  // Controlled_Buffer controlled_buffer_2
  Adder adder_1 (.a(IAR_IN), .b(controlled_buffer_1_out), .out(out_4), .cin(1'b0));  // open: cout
endmodule

module \控制器  (
  input  T,
  input  Clear,
  input  SW,
  input  [7:0] IR,
  output [4:0] \内存控制 ,
  output [5:0] \取值控制 ,
  output [5:0] \UBS控制 ,
  output [6:0] \AUL计算控制 ,
  output [7:0] \RF存储器控制 ,
  output [3:0] \控制字段 ,
  output [5:0] \地址转移 
);

  wire and_1_out, and_2_out, and_3_out, and_4_out, and_5_out, and_6_out, not_1_out, not_2_out, not_3_out,
       or_3_out, or_5_out;
  wire [5:0] or_1_out, register_1_q;

  ROM #(.addrWidth(6), .dataWidth(5)) rom_1 (.addr(register_1_q), .data(\内存控制 ));  // open: sel
  or or_1 (or_1_out[0], \地址转移 [0], and_1_out);
  and and_1 (and_1_out, IR[4], \控制字段 [0]);
  or or_2 (or_1_out[1], \地址转移 [1], and_2_out);
  or or_3 (or_3_out, \地址转移 [2], and_4_out);
  and and_2 (and_2_out, IR[5], \控制字段 [0]);
  ROM #(.addrWidth(6), .dataWidth(6)) rom_2 (.addr(register_1_q), .data(\取值控制 ));  // open: sel
  or or_4 (or_1_out[3], \地址转移 [3], and_3_out);
  and and_3 (and_3_out, IR[7], \控制字段 [0]);
  and and_4 (and_4_out, IR[6], \控制字段 [0]);
  assign or_1_out[2] = not_1_out ? or_3_out : 1'bz;  // Controlled_Buffer controlled_buffer_1
  ROM #(.addrWidth(6), .dataWidth(6)) rom_3 (.addr(register_1_q), .data(\UBS控制 ));  // open: sel
  Register #(.width(6)) register_1 (
    .D({or_1_out[5], \地址转移 [4], or_1_out[3:0]}), .Q(register_1_q), .clk(T), .clr(Clear));  // open: en
  not not_1 (not_1_out, and_5_out);
  assign or_1_out[2] = and_5_out ? 1'b0 : 1'bz;  // Controlled_Buffer controlled_buffer_2
  ROM #(.addrWidth(6), .dataWidth(7)) rom_4 (.addr(register_1_q), .data(\AUL计算控制 ));  // open: sel
  assign or_1_out[5] = not_2_out ? or_5_out : 1'bz;  // Controlled_Buffer controlled_buffer_3
  or or_5 (or_5_out, \地址转移 [5], and_6_out);
  ROM #(.addrWidth(6), .dataWidth(2)) rom_5 (.addr(register_1_q), .data(\RF存储器控制 [1:0]));  // open: sel
  not not_2 (not_2_out, and_5_out);
  and and_5 (and_5_out, not_3_out, \控制字段 [2]);
  not not_3 (not_3_out, SW);
  and and_6 (and_6_out, \控制字段 [1], SW);
  assign or_1_out[5] = and_5_out ? 1'b0 : 1'bz;  // Controlled_Buffer controlled_buffer_4
  ROM #(.addrWidth(6), .dataWidth(4)) rom_6 (.addr(register_1_q), .data(\控制字段 ));  // open: sel
  ROM #(.addrWidth(6), .dataWidth(6)) rom_7 (.addr(register_1_q), .data(\地址转移 ));  // open: sel

  assign \RF存储器控制 [7:2] = {IR[1:0], IR[3:0]};

  // Notes on the sheet:
  //   停机1111
  //   加法1000 xx xx
  //   装入数据1001
  //   减法1010 xx xx
  //   输出寄存器1011 xx 编号
  //   内存控制
  //   contents of rom_1 (hex, n*v repeats v):
  //   0 1 31*0 4 0 10 18 18 10*0 4
  //   取指控制
  //   contents of rom_2 (hex, n*v repeats v):
  //   9*0 4 30*0 25 7*0 2 5
  //   BUS控制
  //   contents of rom_3 (hex, n*v repeats v):
  //   17*0 8 7*0 8 7*0 10 0 14 14 14 0 0 2 7*0 1 4 7*0 8
  //   contents of rom_4 (hex, n*v repeats v):
  //   8*0 28 0 28 8 4*0 2 7*0 6 31*0 4
  //   ALU计算控制
  //   contents of rom_5 (hex, n*v repeats v):
  //   17*0 1 2 6*0 1 2 22*0 1 2
  //   RF存储器控制
  //   contents of rom_6 (hex, n*v repeats v):
  //   2 36*0 4 0 0 0 1
  //   状态标志位
  //   微地址
  //   contents of rom_7 (hex, n*v repeats v):
  //   1 28 0 0 10 0 0 0 10 30 18 38 0 0 0 3f 11 12 1 5*0 19 1a 1 6*0 22 23 24 25 25 0 0 29 7*0 31 32 1 5*0
  //   39 1 5*0 3f
endmodule
